// Logisim project #Sazid_1911498642_LabAssignment01.circ as structural Verilog: 11 circuits, main circuit main
module main (
);


  // Notes on the sheet:
  //   See allocated name for Assingment
endmodule

module NOT_IC (
  input  in_1,
  input  in_2,
  input  in_3,
  input  in_4,
  input  in_5,
  input  in_6,
  input  in_7,
  input  in_8,
  output out_9,
  output out_10,
  output out_11,
  output out_12,
  output out_13,
  output out_14
);

  not not_1 (out_9, in_2);
  not not_2 (out_10, in_3);
  not not_3 (out_11, in_4);
  not not_4 (out_12, in_5);
  not not_5 (out_13, in_6);
  not not_6 (out_14, in_7);
endmodule

module XOR_IC (
  input  in_1,
  input  in_2,
  input  in_3,
  input  in_4,
  input  in_5,
  input  in_6,
  input  in_7,
  input  in_8,
  input  in_9,
  input  in_10,
  output out_11,
  output out_12,
  output out_13,
  output out_14
);

  xor xor_1 (out_11, in_2, in_3);
  xor xor_2 (out_12, in_4, in_5);
  xor xor_3 (out_13, in_6, in_7);
  xor xor_4 (out_14, in_8, in_9);
endmodule

module OR_GATE (
  input  in_1,
  input  in_2,
  input  in_3,
  input  in_4,
  input  in_5,
  input  in_6,
  input  in_7,
  input  in_8,
  input  in_9,
  input  in_10,
  output out_11,
  output out_12,
  output out_13,
  output out_14
);

  or or_1 (out_11, in_2, in_3);
  or or_2 (out_12, in_4, in_5);
  or or_3 (out_13, in_6, in_7);
  or or_4 (out_14, in_8, in_9);
endmodule

module AND_GATE (
  input  in_1,
  input  in_2,
  input  in_3,
  input  in_4,
  input  in_5,
  input  in_6,
  input  in_7,
  input  in_8,
  input  in_9,
  input  in_10,
  output out_11,
  output out_12,
  output out_13,
  output out_14
);

  and and_1 (out_11, in_2, in_3);
  and and_2 (out_12, in_4, in_5);
  and and_3 (out_13, in_6, in_7);
  and and_4 (out_14, in_8, in_9);
endmodule

module MUX (
  input  in_1,
  input  in_2,
  input  in_3,
  input  in_4,
  input  in_5,
  input  in_6,
  output out_7
);

  wire and_1_out, and_2_out, and_3_out, and_4_out, not_1_out, not_2_out;

  not not_1 (not_1_out, in_5);
  not not_2 (not_2_out, in_6);
  and and_1 (and_1_out, in_1, not_1_out, not_2_out);
  and and_2 (and_2_out, in_2, not_1_out, in_6);
  and and_3 (and_3_out, in_3, in_5, not_2_out);
  and and_4 (and_4_out, in_4, in_5, in_6);
  or or_1 (out_7, and_1_out, and_2_out, and_3_out, and_4_out);
endmodule

module D_Flip_Flop (
  input  Set,
  input  in_2,
  input  Data,
  input  Reset,
  output out_5,
  output out_6
);

  wire nand_1_out, nand_2_out, nand_3_out, nand_4_out, not_1_out, not_2_out;

  not not_1 (not_1_out, Set);
  not not_2 (not_2_out, Reset);
  nand nand_1 (nand_1_out, not_1_out, nand_4_out, nand_2_out);
  nand nand_2 (nand_2_out, nand_1_out, in_2, not_2_out);
  nand nand_3 (nand_3_out, nand_2_out, in_2, nand_4_out);
  nand nand_4 (nand_4_out, nand_3_out, Data, not_2_out);
  nand nand_5 (out_5, not_1_out, nand_2_out, out_6);
  nand nand_6 (out_6, out_5, nand_3_out, not_2_out);
endmodule

module _4_bit_adder (
  input  Cin,
  input  B4,
  input  B3,
  input  B2,
  input  B1,
  input  A4,
  input  A3,
  input  A2,
  input  A1,
  output Cout,
  output S4,
  output S3,
  output S2,
  output S1
);

  wire and_1_out, and_2_out, and_3_out, and_4_out, and_5_out, and_6_out, and_7_out, and_8_out, or_1_out,
       or_2_out, or_3_out, xor_1_out, xor_2_out, xor_3_out, xor_4_out;

  xor xor_1 (xor_1_out, A1, B1);
  and and_1 (and_1_out, A1, B1);
  xor xor_2 (xor_2_out, A2, B2);
  and and_2 (and_2_out, A2, B2);
  xor xor_3 (xor_3_out, A3, B3);
  and and_3 (and_3_out, A3, B3);
  xor xor_4 (xor_4_out, A4, B4);
  and and_4 (and_4_out, A4, B4);
  xor xor_5 (S1, xor_1_out, Cin);
  and and_5 (and_5_out, xor_1_out, Cin);
  xor xor_6 (S2, xor_2_out, or_1_out);
  and and_6 (and_6_out, xor_2_out, or_1_out);
  xor xor_7 (S3, xor_3_out, or_2_out);
  and and_7 (and_7_out, xor_3_out, or_2_out);
  xor xor_8 (S4, xor_4_out, or_3_out);
  and and_8 (and_8_out, xor_4_out, or_3_out);
  or or_1 (or_1_out, and_5_out, and_1_out);
  or or_2 (or_2_out, and_6_out, and_2_out);
  or or_3 (or_3_out, and_7_out, and_3_out);
  or or_4 (Cout, and_8_out, and_4_out);
endmodule

module _8_bit_adder (
  input  B7,
  input  B6,
  input  B5,
  input  B4,
  input  B3,
  input  B2,
  input  B1,
  input  B0,
  input  A7,
  input  A6,
  input  A5,
  input  A4,
  input  A3,
  input  A2,
  input  A1,
  input  A0,
  input  Cin,
  output S0,
  output S1,
  output S2,
  output S3,
  output S4,
  output S5,
  output S6,
  output S7,
  output Cout
);

  wire and_1_out, and_2_out, and_3_out, and_4_out, and_5_out, and_6_out, and_7_out, and_8_out, and_9_out,
       and_10_out, and_11_out, and_12_out, and_13_out, and_14_out, and_15_out, and_16_out, or_1_out,
       or_2_out, or_3_out, or_4_out, or_5_out, or_6_out, or_7_out, xor_1_out, xor_2_out, xor_3_out,
       xor_4_out, xor_6_out, xor_7_out, xor_8_out, xor_9_out;

  xor xor_1 (xor_1_out, A0, B0);
  and and_1 (and_1_out, A0, B0);
  xor xor_2 (xor_2_out, A1, B1);
  and and_2 (and_2_out, A1, B1);
  xor xor_3 (xor_3_out, A2, B2);
  and and_3 (and_3_out, A2, B2);
  xor xor_4 (xor_4_out, A3, B3);
  and and_4 (and_4_out, A3, B3);
  xor xor_5 (S0, xor_1_out, Cin);
  and and_5 (and_5_out, xor_1_out, Cin);
  xor xor_6 (xor_6_out, A4, B4);
  and and_6 (and_6_out, A4, B4);
  xor xor_7 (xor_7_out, A5, B5);
  and and_7 (and_7_out, A5, B5);
  xor xor_8 (xor_8_out, A6, B6);
  and and_8 (and_8_out, A6, B6);
  xor xor_9 (xor_9_out, A7, B7);
  and and_9 (and_9_out, A7, B7);
  xor xor_10 (S1, xor_2_out, or_1_out);
  and and_10 (and_10_out, xor_2_out, or_1_out);
  xor xor_11 (S2, xor_3_out, or_2_out);
  and and_11 (and_11_out, xor_3_out, or_2_out);
  xor xor_12 (S3, xor_4_out, or_3_out);
  and and_12 (and_12_out, xor_4_out, or_3_out);
  xor xor_13 (S4, xor_6_out, or_4_out);
  and and_13 (and_13_out, xor_6_out, or_4_out);
  xor xor_14 (S5, xor_7_out, or_5_out);
  and and_14 (and_14_out, xor_7_out, or_5_out);
  or or_1 (or_1_out, and_5_out, and_1_out);
  or or_2 (or_2_out, and_10_out, and_2_out);
  or or_3 (or_3_out, and_11_out, and_3_out);
  xor xor_15 (S6, xor_8_out, or_6_out);
  and and_15 (and_15_out, xor_8_out, or_6_out);
  xor xor_16 (S7, xor_9_out, or_7_out);
  and and_16 (and_16_out, xor_9_out, or_7_out);
  or or_4 (or_4_out, and_12_out, and_4_out);
  or or_5 (or_5_out, and_13_out, and_6_out);
  or or_6 (or_6_out, and_14_out, and_7_out);
  or or_7 (or_7_out, and_15_out, and_8_out);
  or or_8 (Cout, and_16_out, and_9_out);
endmodule

module _8_bit___Combinational_Multiplier (
  input  A8,
  input  A7,
  input  A6,
  input  A5,
  input  A4,
  input  A3,
  input  A2,
  input  A1,
  input  B8,
  input  B7,
  input  B6,
  input  B5,
  input  B4,
  input  B3,
  input  B2,
  input  B1,
  output [15:0] Output
);

  wire C1, C2, C3, C4, C5, C6, C7, C8, E1, E2, E3, E4, E5, E6, E7, E8, n8_bit_adder_2_cout,
       n8_bit_adder_2_s1, n8_bit_adder_2_s2, n8_bit_adder_2_s3, n8_bit_adder_2_s4, n8_bit_adder_2_s5,
       n8_bit_adder_2_s6, n8_bit_adder_2_s7, n8_bit_adder_3_cout, n8_bit_adder_3_s1, n8_bit_adder_3_s2,
       n8_bit_adder_3_s3, n8_bit_adder_3_s4, n8_bit_adder_3_s5, n8_bit_adder_3_s6, n8_bit_adder_3_s7,
       n8_bit_adder_4_cout, n8_bit_adder_4_s1, n8_bit_adder_4_s2, n8_bit_adder_4_s3, n8_bit_adder_4_s4,
       n8_bit_adder_4_s5, n8_bit_adder_4_s6, n8_bit_adder_4_s7, n8_bit_adder_5_cout, n8_bit_adder_5_s1,
       n8_bit_adder_5_s2, n8_bit_adder_5_s3, n8_bit_adder_5_s4, n8_bit_adder_5_s5, n8_bit_adder_5_s6,
       n8_bit_adder_5_s7, n8_bit_adder_6_cout, n8_bit_adder_6_s1, n8_bit_adder_6_s2, n8_bit_adder_6_s3,
       n8_bit_adder_6_s4, n8_bit_adder_6_s5, n8_bit_adder_6_s6, n8_bit_adder_6_s7, n8_bit_adder_7_cout,
       n8_bit_adder_7_s1, n8_bit_adder_7_s2, n8_bit_adder_7_s3, n8_bit_adder_7_s4, n8_bit_adder_7_s5,
       n8_bit_adder_7_s6, n8_bit_adder_7_s7, Q1, Q2, Q3, Q4, Q5, Q6, Q7, Q8, R1, R2, R3, R4, R5, R6, R7, R8,
       T1, T2, T3, T4, T5, T6, T7, T8, V1, V2, V3, V4, V5, V6, V7, V8, X1, X2, X3, X4, X5, X6, X7, X8, Z1,
       Z2, Z3, Z4, Z5, Z6, Z7;

  AND_GATE and_gate_1 (
    .in_2(A1), .in_3(B1), .in_4(A1), .in_5(B2), .in_6(B4), .in_7(A1), .in_8(A1), .in_9(B3),
    .out_11(Output[0]), .out_12(Z1), .out_13(Z3), .out_14(Z2));  // open: in_1, in_10
  AND_GATE and_gate_2 (
    .in_2(A5), .in_3(B1), .in_4(A5), .in_5(B2), .in_6(B4), .in_7(A5), .in_8(A5), .in_9(B3), .out_11(Q1),
    .out_12(Q2), .out_13(Q4), .out_14(Q3));  // open: in_1, in_10
  // Probe on Output
  AND_GATE and_gate_3 (
    .in_2(A1), .in_3(B5), .in_4(A1), .in_5(B6), .in_6(B8), .in_7(A1), .in_8(A1), .in_9(B7), .out_11(Z4),
    .out_12(Z5), .out_13(Z7), .out_14(Z6));  // open: in_1, in_10
  AND_GATE and_gate_4 (
    .in_2(A5), .in_3(B5), .in_4(A5), .in_5(B6), .in_6(B8), .in_7(A5), .in_8(A5), .in_9(B7), .out_11(Q5),
    .out_12(Q6), .out_13(Q8), .out_14(Q7));  // open: in_1, in_10
  // Probe on {A8, A7, A6, A5, A4, A3, A2, A1}
  _8_bit_adder u_8_bit_adder_1 (
    .S0(Output[7]), .S1(Output[8]), .S2(Output[9]), .S3(Output[10]), .S4(Output[11]), .S5(Output[12]),
    .S6(Output[13]), .S7(Output[14]), .Cout(Output[15]), .A7(n8_bit_adder_2_cout), .A6(n8_bit_adder_2_s7),
    .A5(n8_bit_adder_2_s6), .A4(n8_bit_adder_2_s5), .A3(n8_bit_adder_2_s4), .A2(n8_bit_adder_2_s3),
    .A1(n8_bit_adder_2_s2), .A0(n8_bit_adder_2_s1), .B7(R8), .B6(R7), .B5(R6), .B4(R5), .B3(R4), .B2(R3),
    .B1(R2), .B0(R1), .Cin(1'b0));
  AND_GATE and_gate_5 (
    .in_2(A2), .in_3(B1), .in_4(A2), .in_5(B2), .in_6(B4), .in_7(A2), .in_8(A2), .in_9(B3), .out_11(X1),
    .out_12(X2), .out_13(X4), .out_14(X3));  // open: in_1, in_10
  AND_GATE and_gate_6 (
    .in_2(A6), .in_3(B1), .in_4(A6), .in_5(B2), .in_6(B4), .in_7(A6), .in_8(A6), .in_9(B3), .out_11(T1),
    .out_12(T2), .out_13(T4), .out_14(T3));  // open: in_1, in_10
  _8_bit_adder u_8_bit_adder_2 (
    .S0(Output[6]), .S1(n8_bit_adder_2_s1), .S2(n8_bit_adder_2_s2), .S3(n8_bit_adder_2_s3),
    .S4(n8_bit_adder_2_s4), .S5(n8_bit_adder_2_s5), .S6(n8_bit_adder_2_s6), .S7(n8_bit_adder_2_s7),
    .Cout(n8_bit_adder_2_cout), .A7(n8_bit_adder_3_cout), .A6(n8_bit_adder_3_s7), .A5(n8_bit_adder_3_s6),
    .A4(n8_bit_adder_3_s5), .A3(n8_bit_adder_3_s4), .A2(n8_bit_adder_3_s3), .A1(n8_bit_adder_3_s2),
    .A0(n8_bit_adder_3_s1), .B7(E8), .B6(E7), .B5(E6), .B4(E5), .B3(E4), .B2(E3), .B1(E2), .B0(E1), .Cin(1'b0));
  // Probe on {B8, B7, B6, B5, B4, B3, B2, B1}
  _8_bit_adder u_8_bit_adder_3 (
    .S0(Output[5]), .S1(n8_bit_adder_3_s1), .S2(n8_bit_adder_3_s2), .S3(n8_bit_adder_3_s3),
    .S4(n8_bit_adder_3_s4), .S5(n8_bit_adder_3_s5), .S6(n8_bit_adder_3_s6), .S7(n8_bit_adder_3_s7),
    .Cout(n8_bit_adder_3_cout), .A7(n8_bit_adder_4_cout), .A6(n8_bit_adder_4_s7), .A5(n8_bit_adder_4_s6),
    .A4(n8_bit_adder_4_s5), .A3(n8_bit_adder_4_s4), .A2(n8_bit_adder_4_s3), .A1(n8_bit_adder_4_s2),
    .A0(n8_bit_adder_4_s1), .B7(T8), .B6(T7), .B5(T6), .B4(T5), .B3(T4), .B2(T3), .B1(T2), .B0(T1), .Cin(1'b0));
  AND_GATE and_gate_7 (
    .in_2(A2), .in_3(B5), .in_4(A2), .in_5(B6), .in_6(B8), .in_7(A2), .in_8(A2), .in_9(B7), .out_11(X5),
    .out_12(X6), .out_13(X8), .out_14(X7));  // open: in_1, in_10
  AND_GATE and_gate_8 (
    .in_2(A6), .in_3(B5), .in_4(A6), .in_5(B6), .in_6(B8), .in_7(A6), .in_8(A6), .in_9(B7), .out_11(T5),
    .out_12(T6), .out_13(T8), .out_14(T7));  // open: in_1, in_10
  _8_bit_adder u_8_bit_adder_4 (
    .S0(Output[4]), .S1(n8_bit_adder_4_s1), .S2(n8_bit_adder_4_s2), .S3(n8_bit_adder_4_s3),
    .S4(n8_bit_adder_4_s4), .S5(n8_bit_adder_4_s5), .S6(n8_bit_adder_4_s6), .S7(n8_bit_adder_4_s7),
    .Cout(n8_bit_adder_4_cout), .A7(n8_bit_adder_5_cout), .A6(n8_bit_adder_5_s7), .A5(n8_bit_adder_5_s6),
    .A4(n8_bit_adder_5_s5), .A3(n8_bit_adder_5_s4), .A2(n8_bit_adder_5_s3), .A1(n8_bit_adder_5_s2),
    .A0(n8_bit_adder_5_s1), .B7(Q8), .B6(Q7), .B5(Q6), .B4(Q5), .B3(Q4), .B2(Q3), .B1(Q2), .B0(Q1), .Cin(1'b0));
  _8_bit_adder u_8_bit_adder_5 (
    .S0(Output[3]), .S1(n8_bit_adder_5_s1), .S2(n8_bit_adder_5_s2), .S3(n8_bit_adder_5_s3),
    .S4(n8_bit_adder_5_s4), .S5(n8_bit_adder_5_s5), .S6(n8_bit_adder_5_s6), .S7(n8_bit_adder_5_s7),
    .Cout(n8_bit_adder_5_cout), .A7(n8_bit_adder_6_cout), .A6(n8_bit_adder_6_s7), .A5(n8_bit_adder_6_s6),
    .A4(n8_bit_adder_6_s5), .A3(n8_bit_adder_6_s4), .A2(n8_bit_adder_6_s3), .A1(n8_bit_adder_6_s2),
    .A0(n8_bit_adder_6_s1), .B7(V8), .B6(V7), .B5(V6), .B4(V5), .B3(V4), .B2(V3), .B1(V2), .B0(V1), .Cin(1'b0));
  AND_GATE and_gate_9 (
    .in_2(A3), .in_3(B1), .in_4(A3), .in_5(B2), .in_6(B4), .in_7(A3), .in_8(A3), .in_9(B3), .out_11(C1),
    .out_12(C2), .out_13(C4), .out_14(C3));  // open: in_1, in_10
  AND_GATE and_gate_10 (
    .in_2(A7), .in_3(B1), .in_4(A7), .in_5(B2), .in_6(B4), .in_7(A7), .in_8(A7), .in_9(B3), .out_11(E1),
    .out_12(E2), .out_13(E4), .out_14(E3));  // open: in_1, in_10
  _8_bit_adder u_8_bit_adder_6 (
    .S0(Output[2]), .S1(n8_bit_adder_6_s1), .S2(n8_bit_adder_6_s2), .S3(n8_bit_adder_6_s3),
    .S4(n8_bit_adder_6_s4), .S5(n8_bit_adder_6_s5), .S6(n8_bit_adder_6_s6), .S7(n8_bit_adder_6_s7),
    .Cout(n8_bit_adder_6_cout), .A7(n8_bit_adder_7_cout), .A6(n8_bit_adder_7_s7), .A5(n8_bit_adder_7_s6),
    .A4(n8_bit_adder_7_s5), .A3(n8_bit_adder_7_s4), .A2(n8_bit_adder_7_s3), .A1(n8_bit_adder_7_s2),
    .A0(n8_bit_adder_7_s1), .B7(C8), .B6(C7), .B5(C6), .B4(C5), .B3(C4), .B2(C3), .B1(C2), .B0(C1), .Cin(1'b0));
  _8_bit_adder u_8_bit_adder_7 (
    .S0(Output[1]), .S1(n8_bit_adder_7_s1), .S2(n8_bit_adder_7_s2), .S3(n8_bit_adder_7_s3),
    .S4(n8_bit_adder_7_s4), .S5(n8_bit_adder_7_s5), .S6(n8_bit_adder_7_s6), .S7(n8_bit_adder_7_s7),
    .Cout(n8_bit_adder_7_cout), .A7(1'b0), .A6(Z7), .A5(Z6), .A4(Z5), .A3(Z4), .A2(Z3), .A1(Z2), .A0(Z1),
    .B7(X8), .B6(X7), .B5(X6), .B4(X5), .B3(X4), .B2(X3), .B1(X2), .B0(X1), .Cin(1'b0));
  AND_GATE and_gate_11 (
    .in_2(A3), .in_3(B5), .in_4(A3), .in_5(B6), .in_6(B8), .in_7(A3), .in_8(A3), .in_9(B7), .out_11(C5),
    .out_12(C6), .out_13(C8), .out_14(C7));  // open: in_1, in_10
  AND_GATE and_gate_12 (
    .in_2(A7), .in_3(B5), .in_4(A7), .in_5(B6), .in_6(B8), .in_7(A7), .in_8(A7), .in_9(B7), .out_11(E5),
    .out_12(E6), .out_13(E8), .out_14(E7));  // open: in_1, in_10
  AND_GATE and_gate_13 (
    .in_2(A4), .in_3(B1), .in_4(A4), .in_5(B2), .in_6(B4), .in_7(A4), .in_8(A4), .in_9(B3), .out_11(V1),
    .out_12(V2), .out_13(V4), .out_14(V3));  // open: in_1, in_10
  AND_GATE and_gate_14 (
    .in_2(A8), .in_3(B1), .in_4(A8), .in_5(B2), .in_6(B4), .in_7(A8), .in_8(A8), .in_9(B3), .out_11(R1),
    .out_12(R2), .out_13(R4), .out_14(R3));  // open: in_1, in_10
  AND_GATE and_gate_15 (
    .in_2(A4), .in_3(B5), .in_4(A4), .in_5(B6), .in_6(B8), .in_7(A4), .in_8(A4), .in_9(B7), .out_11(V5),
    .out_12(V6), .out_13(V8), .out_14(V7));  // open: in_1, in_10
  AND_GATE and_gate_16 (
    .in_2(A8), .in_3(B5), .in_4(A8), .in_5(B6), .in_6(B8), .in_7(A8), .in_8(A8), .in_9(B7), .out_11(R5),
    .out_12(R6), .out_13(R8), .out_14(R7));  // open: in_1, in_10

  // Other names for the same wires on the sheet: S1 = Output[0]; S2 = Output[1]; S3 = Output[2]; S4 = Output[3];
  //   S5 = Output[4]; S6 = Output[5]; S7 = Output[6]; S8 = Output[7]; S9 = Output[8]; S10 = Output[9];
  //   S11 = Output[10]; S12 = Output[11]; S13 = Output[12]; S14 = Output[13]; S15 = Output[14]; S16 = Output[15]
endmodule

module _4_bit_Logic_Unit (
  input  A3,
  input  A2,
  input  A1,
  input  A0,
  input  B3,
  input  B2,
  input  B1,
  input  B0,
  input  S1,
  input  S0,
  output F4,
  output F3,
  output F2,
  output F1
);

  wire And0, And1, And2, And3, NOT_A0, NOT_A1, NOT_A2, NOT_A3, Or0, Or1, Or2, Or3, Xor0, Xor1, Xor2, Xor3;

  // Probe on {A3, A2, A1, A0}
  Hex_Digit_Display hex_digit_display_1 (.value({A3, A2, A1, A0}));  // open: dp
  AND_GATE and_gate_1 (
    .in_2(A0), .in_3(B0), .in_4(A1), .in_5(B1), .in_6(B3), .in_7(A3), .in_8(A2), .in_9(B2), .out_11(And0),
    .out_12(And1), .out_13(And3), .out_14(And2));  // open: in_1, in_10
  XOR_IC xor_ic_1 (
    .in_2(A0), .in_3(B0), .out_11(Xor0), .in_4(A1), .out_12(Xor1), .in_5(B1), .in_6(A3), .out_13(Xor3),
    .in_7(B3), .in_8(A2), .out_14(Xor2), .in_9(B2));  // open: in_1, in_10
  OR_GATE or_gate_1 (
    .out_11(Or0), .in_2(A0), .in_3(B0), .in_4(A1), .out_12(Or1), .in_5(B1), .in_6(B3), .out_13(Or3),
    .in_7(A3), .in_8(B2), .out_14(Or2), .in_9(A2));  // open: in_1, in_10
  // Probe on {B3, B2, B1, B0}
  Hex_Digit_Display hex_digit_display_2 (.value({B3, B2, B1, B0}));  // open: dp
  Hex_Digit_Display hex_digit_display_3 (.value({F4, F3, F2, F1}));  // open: dp
  // Probe on {F4, F3, F2, F1}
  MUX mux_1 (.in_1(And0), .in_2(Or0), .in_3(Xor0), .in_4(NOT_A0), .out_7(F1), .in_5(S1), .in_6(S0));
  MUX mux_2 (.in_1(And1), .in_2(Or1), .in_3(Xor1), .in_4(NOT_A1), .out_7(F2), .in_5(S1), .in_6(S0));
  MUX mux_3 (.in_1(And2), .in_2(Or2), .in_3(Xor2), .in_4(NOT_A2), .out_7(F3), .in_5(S1), .in_6(S0));
  MUX mux_4 (.in_1(And3), .in_2(Or3), .in_3(Xor3), .in_4(NOT_A3), .out_7(F4), .in_5(S1), .in_6(S0));
  NOT_IC not_ic_1 (
    .in_2(A0), .in_3(A1), .in_4(A2), .in_7(A3), .out_9(NOT_A0), .out_10(NOT_A1), .out_11(NOT_A2),
    .out_14(NOT_A3));  // open: in_1, in_5, in_6, in_8, out_12, out_13
endmodule
