// Logisim project #Sazid_1911498642_lab01.circ as structural Verilog: 8 circuits, main circuit main
module main (
  input  A1,
  input  B1,
  input  A2,
  input  B2,
  input  S1,
  input  S0,
  output F1,
  output F2
);

  wire and_gate_1_out_11, and_gate_1_out_12, not_ic_1_out_9, not_ic_1_out_10, or_gate_1_out_11,
       or_gate_1_out_12, xor_ic_1_out_11, xor_ic_1_out_12;

  AND_GATE and_gate_1 (
    .in_2(A1), .in_3(B1), .in_4(A2), .in_5(B2), .out_11(and_gate_1_out_11), .out_12(and_gate_1_out_12));  // open: in_1, in_6, in_7, in_8, in_9, in_10, out_13, out_14
  OR_GATE or_gate_1 (
    .out_11(or_gate_1_out_11), .in_2(A1), .in_3(B1), .in_4(A2), .out_12(or_gate_1_out_12), .in_5(B2));  // open: in_6, out_13, in_7, in_8, out_14, in_9, in_1, in_10
  XOR_IC xor_ic_1 (
    .in_2(A1), .in_3(B1), .out_11(xor_ic_1_out_11), .in_4(A2), .out_12(xor_ic_1_out_12), .in_5(B2));  // open: in_6, out_13, in_7, in_8, out_14, in_9, in_1, in_10
  NOT_IC not_ic_1 (
    .in_2(A1), .in_3(A2), .out_9(not_ic_1_out_9), .out_10(not_ic_1_out_10));  // open: in_1, in_4, in_5, in_6, in_7, in_8, out_11, out_12, out_13, out_14
  MUX mux_1 (
    .in_1(and_gate_1_out_11), .in_2(or_gate_1_out_11), .in_3(xor_ic_1_out_11), .in_4(not_ic_1_out_9),
    .out_7(F1), .in_5(S1), .in_6(S0));
  MUX mux_2 (
    .in_1(and_gate_1_out_12), .in_2(or_gate_1_out_12), .in_3(xor_ic_1_out_12), .in_4(not_ic_1_out_10),
    .out_7(F2), .in_5(S1), .in_6(S0));
endmodule

module NOT_IC (
  input  in_1,
  input  in_2,
  input  in_3,
  input  in_4,
  input  in_5,
  input  in_6,
  input  in_7,
  input  in_8,
  output out_9,
  output out_10,
  output out_11,
  output out_12,
  output out_13,
  output out_14
);

  not not_1 (out_9, in_2);
  not not_2 (out_10, in_3);
  not not_3 (out_11, in_4);
  not not_4 (out_12, in_5);
  not not_5 (out_13, in_6);
  not not_6 (out_14, in_7);
endmodule

module XOR_IC (
  input  in_1,
  input  in_2,
  input  in_3,
  input  in_4,
  input  in_5,
  input  in_6,
  input  in_7,
  input  in_8,
  input  in_9,
  input  in_10,
  output out_11,
  output out_12,
  output out_13,
  output out_14
);

  xor xor_1 (out_11, in_2, in_3);
  xor xor_2 (out_12, in_4, in_5);
  xor xor_3 (out_13, in_6, in_7);
  xor xor_4 (out_14, in_8, in_9);
endmodule

module OR_GATE (
  input  in_1,
  input  in_2,
  input  in_3,
  input  in_4,
  input  in_5,
  input  in_6,
  input  in_7,
  input  in_8,
  input  in_9,
  input  in_10,
  output out_11,
  output out_12,
  output out_13,
  output out_14
);

  or or_1 (out_11, in_2, in_3);
  or or_2 (out_12, in_4, in_5);
  or or_3 (out_13, in_6, in_7);
  or or_4 (out_14, in_8, in_9);
endmodule

module AND_GATE (
  input  in_1,
  input  in_2,
  input  in_3,
  input  in_4,
  input  in_5,
  input  in_6,
  input  in_7,
  input  in_8,
  input  in_9,
  input  in_10,
  output out_11,
  output out_12,
  output out_13,
  output out_14
);

  and and_1 (out_11, in_2, in_3);
  and and_2 (out_12, in_4, in_5);
  and and_3 (out_13, in_6, in_7);
  and and_4 (out_14, in_8, in_9);
endmodule

module MUX (
  input  in_1,
  input  in_2,
  input  in_3,
  input  in_4,
  input  in_5,
  input  in_6,
  output out_7
);

  wire and_1_out, and_2_out, and_3_out, and_4_out, not_1_out, not_2_out;

  not not_1 (not_1_out, in_6);
  not not_2 (not_2_out, in_5);
  and and_1 (and_1_out, in_1, not_2_out, not_1_out);
  and and_2 (and_2_out, in_2, not_2_out, in_6);
  and and_3 (and_3_out, in_3, in_5, not_1_out);
  and and_4 (and_4_out, in_4, in_5, in_6);
  or or_1 (out_7, and_1_out, and_2_out, and_3_out, and_4_out);
endmodule

module D_Flip_Flop (
  input  Set,
  input  in_2,
  input  Data,
  input  Reset,
  output out_5,
  output out_6
);

  wire nand_1_out, nand_2_out, nand_3_out, nand_4_out, not_1_out, not_2_out;

  not not_1 (not_1_out, Set);
  not not_2 (not_2_out, Reset);
  nand nand_1 (nand_1_out, not_1_out, nand_4_out, nand_2_out);
  nand nand_2 (nand_2_out, nand_1_out, in_2, not_2_out);
  nand nand_3 (nand_3_out, nand_2_out, in_2, nand_4_out);
  nand nand_4 (nand_4_out, nand_3_out, Data, not_2_out);
  nand nand_5 (out_5, not_1_out, nand_2_out, out_6);
  nand nand_6 (out_6, out_5, nand_3_out, not_2_out);
endmodule

module _4_bit_adder (
  input  Cin,
  input  B4,
  input  B3,
  input  B2,
  input  B1,
  input  A4,
  input  A3,
  input  A2,
  input  A1,
  output Cout,
  output S4,
  output S3,
  output S2,
  output S1
);

  wire and_1_out, and_2_out, and_3_out, and_4_out, and_5_out, and_6_out, and_7_out, and_8_out, or_1_out,
       or_2_out, or_3_out, xor_1_out, xor_2_out, xor_3_out, xor_4_out;

  xor xor_1 (xor_1_out, A1, B1);
  and and_1 (and_1_out, A1, B1);
  xor xor_2 (xor_2_out, A2, B2);
  and and_2 (and_2_out, A2, B2);
  xor xor_3 (xor_3_out, A3, B3);
  and and_3 (and_3_out, A3, B3);
  xor xor_4 (xor_4_out, A4, B4);
  and and_4 (and_4_out, A4, B4);
  xor xor_5 (S1, xor_1_out, Cin);
  and and_5 (and_5_out, xor_1_out, Cin);
  xor xor_6 (S2, xor_2_out, or_1_out);
  and and_6 (and_6_out, xor_2_out, or_1_out);
  xor xor_7 (S3, xor_3_out, or_2_out);
  and and_7 (and_7_out, xor_3_out, or_2_out);
  xor xor_8 (S4, xor_4_out, or_3_out);
  and and_8 (and_8_out, xor_4_out, or_3_out);
  or or_1 (or_1_out, and_5_out, and_1_out);
  or or_2 (or_2_out, and_6_out, and_2_out);
  or or_3 (or_3_out, and_7_out, and_3_out);
  or or_4 (Cout, and_8_out, and_4_out);
endmodule
