// Logisim project #Sazid_1911498642_lab06.circ as structural Verilog: 4 circuits, main circuit main
module main (
  input  [15:0] in_1,
  input  in_2,
  input  [15:0] in_3,
  input  [1:0] in_4,
  output [15:0] out_5,
  output out_6,
  output out_7
);

  _16_bit_ALU u_16_bit_alu_1 (
    .A(in_1), .C(out_5), .B(in_3), .Zero(out_6), .Operation(in_4), .Overflow(out_7), .SUB(in_2),
    .Binvert(1'b0), .Ainvert(in_2));  // open: Cout
endmodule

module _16_Bit_Register (
  input  Write,
  input  [3:0] Read_Register_1,
  input  [3:0] Read_Register_2,
  input  [3:0] Write_Register,
  input  [15:0] Write_Data,
  input  Clock,
  output [15:0] Read_Data_1,
  output [15:0] Read_Data_2
);

  wire and_1_out, and_2_out, and_3_out, and_4_out, and_5_out, and_6_out, and_7_out, and_8_out, and_9_out,
       and_10_out, and_11_out, and_12_out, and_13_out, and_14_out, and_15_out, and_16_out, decoder_1_out0,
       decoder_1_out1, decoder_1_out2, decoder_1_out3, decoder_1_out4, decoder_1_out5, decoder_1_out6,
       decoder_1_out7, decoder_1_out8, decoder_1_out9, decoder_1_out10, decoder_1_out11, decoder_1_out12,
       decoder_1_out13, decoder_1_out14, decoder_1_out15;
  wire [15:0] register_1_q, register_2_q, register_3_q, register_4_q, register_5_q, register_6_q,
       register_7_q, register_8_q, register_9_q, register_10_q, register_11_q, register_12_q, register_13_q,
       register_14_q, register_15_q, register_16_q;

  Decoder #(.select(4)) decoder_1 (
    .out0(decoder_1_out0), .out1(decoder_1_out1), .out2(decoder_1_out2), .out3(decoder_1_out3),
    .out4(decoder_1_out4), .out5(decoder_1_out5), .out6(decoder_1_out6), .out7(decoder_1_out7),
    .out8(decoder_1_out8), .out9(decoder_1_out9), .out10(decoder_1_out10), .out11(decoder_1_out11),
    .out12(decoder_1_out12), .out13(decoder_1_out13), .out14(decoder_1_out14), .out15(decoder_1_out15),
    .sel(Write_Register));  // open: en
  and and_1 (and_1_out, decoder_1_out0, Write);
  and and_2 (and_2_out, decoder_1_out1, Write);
  and and_3 (and_3_out, decoder_1_out2, Write);
  and and_4 (and_4_out, decoder_1_out3, Write);
  and and_5 (and_5_out, decoder_1_out4, Write);
  and and_6 (and_6_out, decoder_1_out5, Write);
  and and_7 (and_7_out, decoder_1_out6, Write);
  and and_8 (and_8_out, decoder_1_out7, Write);
  Register #(.width(16)) register_1 (.D(Write_Data), .en(and_1_out), .Q(register_1_q), .clk(Clock));  // open: clr
  Register #(.width(16)) register_2 (.D(Write_Data), .en(and_2_out), .Q(register_2_q), .clk(Clock));  // open: clr
  Register #(.width(16)) register_3 (.D(Write_Data), .en(and_3_out), .Q(register_3_q), .clk(Clock));  // open: clr
  Register #(.width(16)) register_4 (.D(Write_Data), .en(and_4_out), .Q(register_4_q), .clk(Clock));  // open: clr
  Register #(.width(16)) register_5 (.D(Write_Data), .en(and_5_out), .Q(register_5_q), .clk(Clock));  // open: clr
  Register #(.width(16)) register_6 (.D(Write_Data), .en(and_6_out), .Q(register_6_q), .clk(Clock));  // open: clr
  Register #(.width(16)) register_7 (.D(Write_Data), .en(and_7_out), .Q(register_7_q), .clk(Clock));  // open: clr
  Register #(.width(16)) register_8 (.D(Write_Data), .en(and_8_out), .Q(register_8_q), .clk(Clock));  // open: clr
  and and_9 (and_9_out, decoder_1_out8, Write);
  and and_10 (and_10_out, decoder_1_out9, Write);
  and and_11 (and_11_out, decoder_1_out10, Write);
  and and_12 (and_12_out, decoder_1_out11, Write);
  and and_13 (and_13_out, decoder_1_out12, Write);
  and and_14 (and_14_out, decoder_1_out13, Write);
  and and_15 (and_15_out, decoder_1_out14, Write);
  and and_16 (and_16_out, decoder_1_out15, Write);
  Register #(.width(16)) register_9 (.D(Write_Data), .en(and_9_out), .Q(register_9_q), .clk(Clock));  // open: clr
  Register #(.width(16)) register_10 (.D(Write_Data), .en(and_10_out), .Q(register_10_q), .clk(Clock));  // open: clr
  Register #(.width(16)) register_11 (.D(Write_Data), .en(and_11_out), .Q(register_11_q), .clk(Clock));  // open: clr
  Register #(.width(16)) register_12 (.D(Write_Data), .en(and_12_out), .Q(register_12_q), .clk(Clock));  // open: clr
  Register #(.width(16)) register_13 (.D(Write_Data), .en(and_13_out), .Q(register_13_q), .clk(Clock));  // open: clr
  Register #(.width(16)) register_14 (.en(and_14_out), .Q(register_14_q), .clk(Clock));  // open: D, clr
  Register #(.width(16)) register_15 (.D(Write_Data), .en(and_15_out), .Q(register_15_q), .clk(Clock));  // open: clr
  Register #(.width(16)) register_16 (.D(Write_Data), .en(and_16_out), .Q(register_16_q), .clk(Clock));  // open: clr
  Multiplexer #(.select(4), .width(16)) multiplexer_1 (
    .in0(register_1_q), .in1(register_2_q), .in2(register_3_q), .in3(register_4_q), .in4(register_5_q),
    .in5(register_6_q), .in6(register_7_q), .in7(register_8_q), .in8(register_9_q), .in9(register_10_q),
    .in10(register_11_q), .in11(register_12_q), .in12(register_13_q), .in13(register_14_q),
    .in14(register_15_q), .in15(register_16_q), .out(Read_Data_1), .sel(Read_Register_1));  // open: en
  Multiplexer #(.select(4), .width(16)) multiplexer_2 (
    .in0(register_1_q), .in1(register_2_q), .in2(register_3_q), .in3(register_4_q), .in4(register_5_q),
    .in5(register_6_q), .in6(register_7_q), .in7(register_8_q), .in8(register_9_q), .in9(register_10_q),
    .in10(register_11_q), .in11(register_12_q), .in12(register_13_q), .in13(register_14_q),
    .in14(register_15_q), .in15(register_16_q), .out(Read_Data_2), .sel(Read_Register_2));  // open: en
endmodule

module _1_bit_ALU (
  input  B,
  input  A,
  input  Sub,
  input  [1:0] Operation,
  input  Binvert,
  input  Ainvert,
  output Result,
  output Carry_Out,
  output Mul_Cout
);

  wire adder_1_out, and_1_out, multiplexer_1_out, multiplexer_2_out, multiplier_1_out, not_1_out, not_2_out,
       or_1_out;

  Multiplexer multiplexer_1 (.in0(B), .in1(not_1_out), .out(multiplexer_1_out), .sel(Binvert));  // open: en
  not not_1 (not_1_out, B);
  Multiplexer multiplexer_2 (.in0(A), .in1(not_2_out), .out(multiplexer_2_out), .sel(Ainvert));  // open: en
  not not_2 (not_2_out, A);
  and and_1 (and_1_out, B, A);
  or or_1 (or_1_out, B, A);
  Adder #(.width(1)) adder_1 (
    .a(multiplexer_1_out), .b(multiplexer_2_out), .out(adder_1_out), .cin(Sub), .cout(Carry_Out));
  Multiplier #(.width(1)) multiplier_1 (.a(A), .b(B), .out(multiplier_1_out), .cout(Mul_Cout));  // open: cin
  Multiplexer #(.select(2)) multiplexer_3 (
    .in0(and_1_out), .in1(or_1_out), .in2(adder_1_out), .in3(multiplier_1_out), .out(Result), .sel(Operation));  // open: en
endmodule

module _16_bit_ALU (
  input  SUB,
  input  [15:0] A,
  input  [15:0] B,
  input  [1:0] Operation,
  input  Binvert,
  input  Ainvert,
  output [15:0] C,
  output Zero,
  output Overflow,
  output Cout
);

  wire n1_bit_alu_1_carry_out, n1_bit_alu_2_carry_out, n1_bit_alu_3_carry_out, n1_bit_alu_4_carry_out,
       n1_bit_alu_5_carry_out, n1_bit_alu_6_carry_out, n1_bit_alu_7_carry_out, n1_bit_alu_9_carry_out,
       n1_bit_alu_10_carry_out, n1_bit_alu_11_carry_out, n1_bit_alu_12_carry_out, n1_bit_alu_13_carry_out,
       n1_bit_alu_14_carry_out, n1_bit_alu_15_carry_out, X;

  _1_bit_ALU u_1_bit_alu_1 (
    .Result(C[0]), .B(B[0]), .A(A[0]), .Sub(SUB), .Operation(Operation), .Binvert(Binvert),
    .Ainvert(Ainvert), .Carry_Out(n1_bit_alu_1_carry_out));  // open: Mul_Cout
  _1_bit_ALU u_1_bit_alu_2 (
    .Result(C[1]), .B(B[1]), .A(A[1]), .Sub(n1_bit_alu_1_carry_out), .Operation(Operation),
    .Binvert(Binvert), .Ainvert(Ainvert), .Carry_Out(n1_bit_alu_2_carry_out));  // open: Mul_Cout
  _1_bit_ALU u_1_bit_alu_3 (
    .Result(C[2]), .B(B[2]), .A(A[2]), .Sub(n1_bit_alu_2_carry_out), .Operation(Operation),
    .Binvert(Binvert), .Ainvert(Ainvert), .Carry_Out(n1_bit_alu_3_carry_out));  // open: Mul_Cout
  _1_bit_ALU u_1_bit_alu_4 (
    .Result(C[3]), .B(B[3]), .A(A[3]), .Sub(n1_bit_alu_3_carry_out), .Operation(Operation),
    .Binvert(Binvert), .Ainvert(Ainvert), .Carry_Out(n1_bit_alu_4_carry_out));  // open: Mul_Cout
  _1_bit_ALU u_1_bit_alu_5 (
    .Result(C[4]), .B(B[4]), .A(A[4]), .Sub(n1_bit_alu_4_carry_out), .Operation(Operation),
    .Binvert(Binvert), .Ainvert(Ainvert), .Carry_Out(n1_bit_alu_5_carry_out));  // open: Mul_Cout
  _1_bit_ALU u_1_bit_alu_6 (
    .Result(C[5]), .B(B[5]), .A(A[5]), .Sub(n1_bit_alu_5_carry_out), .Operation(Operation),
    .Binvert(Binvert), .Ainvert(Ainvert), .Carry_Out(n1_bit_alu_6_carry_out));  // open: Mul_Cout
  _1_bit_ALU u_1_bit_alu_7 (
    .Result(C[6]), .B(B[6]), .A(A[6]), .Sub(n1_bit_alu_6_carry_out), .Operation(Operation),
    .Binvert(Binvert), .Ainvert(Ainvert), .Carry_Out(n1_bit_alu_7_carry_out));  // open: Mul_Cout
  _1_bit_ALU u_1_bit_alu_8 (
    .Result(C[7]), .B(B[7]), .A(A[7]), .Sub(n1_bit_alu_7_carry_out), .Operation(Operation),
    .Binvert(Binvert), .Ainvert(Ainvert), .Carry_Out(X));  // open: Mul_Cout
  _1_bit_ALU u_1_bit_alu_9 (
    .Result(C[8]), .B(B[8]), .A(A[8]), .Sub(X), .Operation(Operation), .Binvert(Binvert), .Ainvert(Ainvert),
    .Carry_Out(n1_bit_alu_9_carry_out));  // open: Mul_Cout
  _1_bit_ALU u_1_bit_alu_10 (
    .Result(C[9]), .B(B[9]), .A(A[9]), .Sub(n1_bit_alu_9_carry_out), .Operation(Operation),
    .Binvert(Binvert), .Ainvert(Ainvert), .Carry_Out(n1_bit_alu_10_carry_out));  // open: Mul_Cout
  _1_bit_ALU u_1_bit_alu_11 (
    .Result(C[10]), .B(B[10]), .A(A[10]), .Sub(n1_bit_alu_10_carry_out), .Operation(Operation),
    .Binvert(Binvert), .Ainvert(Ainvert), .Carry_Out(n1_bit_alu_11_carry_out));  // open: Mul_Cout
  _1_bit_ALU u_1_bit_alu_12 (
    .Result(C[11]), .B(B[11]), .A(A[11]), .Sub(n1_bit_alu_11_carry_out), .Operation(Operation),
    .Binvert(Binvert), .Ainvert(Ainvert), .Carry_Out(n1_bit_alu_12_carry_out));  // open: Mul_Cout
  _1_bit_ALU u_1_bit_alu_13 (
    .Result(C[12]), .B(B[12]), .A(A[12]), .Sub(n1_bit_alu_12_carry_out), .Operation(Operation),
    .Binvert(Binvert), .Ainvert(Ainvert), .Carry_Out(n1_bit_alu_13_carry_out));  // open: Mul_Cout
  _1_bit_ALU u_1_bit_alu_14 (
    .Result(C[13]), .B(B[13]), .A(A[13]), .Sub(n1_bit_alu_13_carry_out), .Operation(Operation),
    .Binvert(Binvert), .Ainvert(Ainvert), .Carry_Out(n1_bit_alu_14_carry_out));  // open: Mul_Cout
  _1_bit_ALU u_1_bit_alu_15 (
    .Result(C[14]), .B(B[14]), .A(A[14]), .Sub(n1_bit_alu_14_carry_out), .Operation(Operation),
    .Binvert(Binvert), .Ainvert(Ainvert), .Carry_Out(n1_bit_alu_15_carry_out));  // open: Mul_Cout
  _1_bit_ALU u_1_bit_alu_16 (
    .Result(C[15]), .B(B[15]), .A(A[15]), .Sub(n1_bit_alu_15_carry_out), .Operation(Operation),
    .Binvert(Binvert), .Ainvert(Ainvert), .Carry_Out(Cout));  // open: Mul_Cout
  nor nor_1 (Zero, C[0], C[1], C[2], C[3], C[4], C[5], C[6], C[7], C[8], C[9], C[10], C[11], C[12], C[13], C[14], C[15]);
  xor xor_1 (Overflow, n1_bit_alu_15_carry_out, Cout);
endmodule
